// Logisim project k16x.circ as structural Verilog: 1 circuit, main circuit main
module main (
);

  wire IOWe, not_1_out, or_1_out, RST;
  wire [3:0] ALUOp;
  wire [15:0] ALUOut, demultiplexer_1_out0, demultiplexer_1_out1, demultiplexer_1_out2, demultiplexer_1_out3,
       demultiplexer_1_out4, demultiplexer_1_out5, demultiplexer_1_out6, demultiplexer_1_out7,
       demultiplexer_3_out0, demultiplexer_3_out1, demultiplexer_3_out2, demultiplexer_3_out3,
       demultiplexer_3_out4, demultiplexer_3_out5, demultiplexer_3_out6, demultiplexer_3_out7, IMM,
       Instruction, IOAddr, IOIn, RegAOut, RegBOut, RegIn;

  Register #(.width(16)) u_Instruction (
    .Q({Instruction[15:10], ALUOp, Instruction[5:0]}), .clr(RST));  // open: D, en, clk
  // Probe on RegAOut
  Demultiplexer #(.select(3), .width(16)) demultiplexer_1 (
    .out0(demultiplexer_1_out0), .out1(demultiplexer_1_out1), .out2(demultiplexer_1_out2),
    .out3(demultiplexer_1_out3), .out4(demultiplexer_1_out4), .out5(demultiplexer_1_out5),
    .out6(demultiplexer_1_out6), .out7(demultiplexer_1_out7), .in(RegAOut), .sel(Instruction[2:0]));
  // Probe on RegBOut
  Demultiplexer #(.select(3), .width(16)) demultiplexer_2 (
    .out0(demultiplexer_1_out0), .out1(demultiplexer_1_out1), .out2(demultiplexer_1_out2),
    .out3(demultiplexer_1_out3), .out4(demultiplexer_1_out4), .out5(demultiplexer_1_out5),
    .out6(demultiplexer_1_out6), .out7(demultiplexer_1_out7), .in(RegBOut), .sel(Instruction[5:3]));
  Register #(.width(16)) x0 (.D(demultiplexer_3_out0), .Q(demultiplexer_1_out0), .clr(RST));  // open: en, clk
  Register #(.width(16)) x1 (.D(demultiplexer_3_out1), .Q(demultiplexer_1_out1), .clr(RST));  // open: en, clk
  Register #(.width(16)) x2 (.D(demultiplexer_3_out2), .Q(demultiplexer_1_out2), .clr(RST));  // open: en, clk
  Register #(.width(16)) x3 (.D(demultiplexer_3_out3), .Q(demultiplexer_1_out3), .clr(RST));  // open: en, clk
  Multiplexer #(.width(16)) multiplexer_1 (.in0(IMM), .in1(RegBOut), .out(IOAddr), .sel(Instruction[15]));
  Register #(.width(16)) x4 (.D(demultiplexer_3_out4), .Q(demultiplexer_1_out4), .clr(RST));  // open: en, clk
  Register #(.width(16)) x5 (.D(demultiplexer_3_out5), .Q(demultiplexer_1_out5), .clr(RST));  // open: en, clk
  Register #(.width(16)) sp (.D(demultiplexer_3_out6), .Q(demultiplexer_1_out6), .clr(RST));  // open: en, clk
  not not_1 (not_1_out, Instruction[12]);
  or or_1 (or_1_out, Instruction[13], Instruction[14]);
  Multiplexer #(.enable("true"), .select(2), .width(16)) multiplexer_2 (
    .in0(ALUOut), .in1(RegBOut), .in2(ALUOut), .in3(IMM), .out(RegIn), .sel(Instruction[14:13]),
    .en(Instruction[12]));
  Multiplexer #(.enable("true"), .select(2), .width(16)) multiplexer_3 (
    .in1(RegAOut), .in2(ALUOut), .in3(IMM), .out(IOIn), .sel(Instruction[14:13]), .en(IOWe));  // open: in0
  and and_1 (IOWe, not_1_out, or_1_out);
  Register #(.width(16)) pc (.D(demultiplexer_3_out7), .Q(demultiplexer_1_out7), .clr(RST));  // open: en, clk
  Demultiplexer #(.select(3), .width(16)) demultiplexer_3 (
    .out0(demultiplexer_3_out0), .out1(demultiplexer_3_out1), .out2(demultiplexer_3_out2),
    .out3(demultiplexer_3_out3), .out4(demultiplexer_3_out4), .out5(demultiplexer_3_out5),
    .out6(demultiplexer_3_out6), .out7(demultiplexer_3_out7), .in(RegIn), .sel(Instruction[2:0]));

  // Other names for the same wires on the sheet: RegASelect[2:0] = Instruction[2:0];
  //   RegBSelect[2:0] = Instruction[5:3]; Instruction[9:6] = ALUOp; RegWE = Instruction[12];
  //   WriteSelect[2:0] = Instruction[14:12]; IOAddrSelect = Instruction[15]
endmodule
